# Fritzing sketch LightningCloud (saved by Fritzing 0.9.3b)
breadboards: 1

parts:
  Arduino_Uno_R3 = Arduino Uno (Rev3)
  Data-In_Resistor = Resistor [tolerance=±5% resistance=470 package=THT]
  C2 = Electrolytic Capacitor [capacitance=1000μF voltage=25V package="1010 [SMD, electrolytic]"]
  NEOPIXEL1 = Neopixel Strip -- Black (60/m) [part_number=1461]
  PSU1 = Adjustable Breadboard Power Supply
  VCC1 = Battery block 9V

nets (from the breadboard view):
  N1: Arduino_Uno_R3.D6_PWM, Data-In_Resistor.Pin_1
  N2: Arduino_Uno_R3.GND, Data-In_Resistor.Pin_0, NEOPIXEL1.DI
  N3: C2.-, NEOPIXEL1.GND, PSU1.Vout-
  N4: C2.+, NEOPIXEL1.+5V, PSU1.Vout+
  N5: PSU1.Vin+, VCC1.+
  N6: PSU1.Vin-, VCC1.-

notes:
  Breadboard power supply output 5V

custom parts:
  Neopixel Strip -- Black (60/m): Neopixel Strip, Black, 60 pixels per meter.
