# Fritzing sketch SoundBoardFX (saved by Fritzing 0.9.3b)

parts:
  Adafruit_SoundBoard_FX = Audio FX Sound Board + 2x2W Amp
  Arduino_Uno = Arduino Uno (Rev3)
  L_Speaker = Piezo Speaker
  R_Speaker = Piezo Speaker

nets:
  VIN: Adafruit_SoundBoard_FX.VIN, Arduino_Uno.3V3
  GND: Adafruit_SoundBoard_FX.GND, Arduino_Uno.GND
  N1: Adafruit_SoundBoard_FX.0, Arduino_Uno.D4
  N2: Adafruit_SoundBoard_FX.L-, L_Speaker.pin1
  N3: Adafruit_SoundBoard_FX.L+, L_Speaker.pin2
  N4: Adafruit_SoundBoard_FX.R+, R_Speaker.pin2
  N5: Adafruit_SoundBoard_FX.R-, R_Speaker.pin1

custom parts:
  Audio FX Sound Board + 2x2W Amp: The Adafruit Sound Board, the fastest way to add audio effects to a project!
